# Fritzing sketch motor_blind (saved by Fritzing 0.8.7b)

parts:
  U1 = NodeMCU V3.0
  MOTOR1 = Adafruit Gear-Reduced Stepper Motor (small)
  9_-_12V_DC = 2.1mm Barrel Jack with Terminal Block
  BREAKOUT1 = ULN2003A breakout board

nets:
  N1: U1.D1, BREAKOUT1.In_1
  N2: U1.D2, BREAKOUT1.In_3
  N3: U1.D3, BREAKOUT1.In_2
  N4: U1.GND, 9_-_12V_DC.NEG, BREAKOUT1.0V
  N5: U1.D5, BREAKOUT1.In_4
  VIN: U1.Vin, 9_-_12V_DC.POS, BREAKOUT1.+5V
  N6: MOTOR1.RED, BREAKOUT1.BLUE_wire
  N7: MOTOR1.ORANGE, BREAKOUT1.PINK_wire
  N8: MOTOR1.YELLOW, BREAKOUT1.YELLOW_wire
  N9: MOTOR1.PINK, BREAKOUT1.ORANGE_wire
  N10: MOTOR1.BLUE, BREAKOUT1.RED_wire

custom parts:
  NodeMCU V3.0: ESP8266 based NodeMCU
  Adafruit Gear-Reduced Stepper Motor (small): Adafruit gear-reduction stepper motor (small)
  ULN2003A breakout board: ULN2003A 7-way Darlington Transistor Driver on breakoutboard
